# Fritzing sketch Sabotage-Detection (saved by Fritzing 0.8.5b)
circuit board: 6.88566cm x 5.36311cm
breadboards: 2

parts:
  Arduino1 = Arduino Uno (Rev3)
  S2 = Pushbutton [package="[THT]"]
  R6 = Resistor [tolerance=±5% resistance=220 package=THT]
  R7 = Resistor [tolerance=±5% resistance=1.1k package=THT]
  R8 = Resistor [tolerance=±5% resistance=220 package=THT]
  R9 = Resistor [tolerance=±5% resistance=220 package=THT]
  LED6 = LED - 5mm [color="Green (555nm)" package="5 mm [THT]"]
  ADXL335 = Triple Axis Accelerometer Breakout - ADXL335
  LED7 = Super Flux LED blue [color=Red]
  LED8 = Super Flux LED blue [color=Blue]
  Pot = Rotary Potentiometer (Small) [maximum_resistance=100kΩ package=THT]

nets:
  N1: Arduino1.A0, ADXL335.ZOUT
  N2: Arduino1.A1, ADXL335.YOUT
  N3: Arduino1.A2, ADXL335.XOUT
  N4: Arduino1.A3, Pot.wiper
  GND: Arduino1.GND, R6.Pin_0, R7.Pin_0, R8.Pin_0, R9.Pin_0, ADXL335.GND, Pot.leg2
  N5: Arduino1.D11_PWM/MOSI, LED6.anode
  N6: Arduino1.D2, S2.Pin_3, S2.Pin_4, R7.Pin_1
  N7: Arduino1.D3_PWM, LED7.anode
  N8: Arduino1.D7, LED8.anode
  3V3: Arduino1.3V3, ADXL335.VCC
  N9: Arduino1.5V, S2.Pin_1, S2.Pin_2, Pot.leg1
  N10: R6.Pin_1, LED6.cathode
  N11: R8.Pin_1, LED7.cathode
  N12: R9.Pin_1, LED8.cathode

notes:
  Get the Arduino Code from here:
  Sabotage Alert
